# Fritzing sketch led-controller (saved by Fritzing 0.9.4)
perfboards: 1

parts:
  J3 = female pin header, 4 pins [form="♀ (female)"]
  J1 = female pin header, 19 pins [form="♀ (female)"]
  J2 = female pin header, 19 pins [form="♀ (female)"]
  R1 = Resistor [tolerance=±5% resistance=4.7k package=THT]
  R2 = Resistor [tolerance=±5% resistance=4.7k package=THT]
  Q4 = NPN-Transistor [package="TO92 [THT]"]
  Q5 = NPN-Transistor [package="TO92 [THT]"]
  Q6 = NPN-Transistor [package="TO92 [THT]"]
  LED_PWM = Camdenboss CTB0158-6 [part_number=CTB0158-6 package=THT]
  LED_Temp = Camdenboss CTB0158-4 [part_number=CTB0158-4 package=THT]
  5v = Camdenboss CTB0158-2 [part_number=CTB0158-2 package=THT]
  24v = Camdenboss CTB0158-2 [part_number=CTB0158-2 package=THT]
  DMX = Camdenboss CTB0158-3 [part_number=CTB0158-3 package=THT]
  Case_Fan = Camdenboss CTB0158-2 [part_number=CTB0158-2 package=THT]
  Q7 = NPN-Transistor [package="TO92 [THT]"]
  R4 = Resistor [tolerance=±5% resistance=4.7k package=THT]
  R5 = Resistor [tolerance=±5% resistance=4.7k package=THT]
  R6 = Resistor [tolerance=±5% resistance=10k package=THT]
  Case_Temp = Camdenboss CTB0158-2 [part_number=CTB0158-2 package=THT]
  R7 = Resistor [tolerance=±5% resistance=10k package=THT]
  R8 = Resistor [tolerance=±5% resistance=10k package=THT]
  R9 = Resistor [tolerance=±5% resistance=10k package=THT]
  LED_Fan = Camdenboss CTB0158-5 [part_number=CTB0158-5 package=THT]
  Q8 = NPN-Transistor [package="TO92 [THT]"]
  Display = Camdenboss CTB0158-4 [part_number=CTB0158-4 package=THT]
  R10 = Resistor [tolerance=±5% resistance=4.7k package=THT]
  U1 = MAX485 [package=dil08]

nets:
  N1: J3.pin1, J2.pin19, DMX.pin3, Display.terminal_4, U1.GND
  N2: J3.pin2, J2.pin8, U1.DI
  N3: J3.pin3, U1.RO
  N4: J3.pin4, J1.pin1, 5v.pin1, Display.terminal_1, U1.VCC
  N5: J1.pin5, R4.Pin_1
  N6: J1.pin6, LED_PWM.terminal_2, LED_PWM.terminal_4, LED_PWM.terminal_6, 5v.pin2, 24v.pin2, Q7.E, R6.Pin_1, R7.Pin_1, R8.Pin_1, R9.Pin_1, LED_Fan.pin1, Q8.E
  N7: J1.pin7, R2.Pin_1
  N8: J1.pin8, R5.Pin_1
  N9: J1.pin9, LED_Fan.pin3
  N10: J1.pin10, LED_Fan.pin4
  N11: J1.pin11, R1.Pin_1
  N12: J1.pin12, LED_Temp.pin1
  N13: J1.pin13, LED_Temp.pin2
  N14: J1.pin14, Case_Temp.terminal_2
  N15: J1.pin15, LED_Temp.pin3
  N16: J1.pin19, LED_Temp.terminal_4, Case_Temp.terminal_1
  N17: J2.pin10, R10.Pin_1
  N18: J2.pin14, Display.terminal_2
  N19: J2.pin17, Display.terminal_3
  N20: R1.Pin_0, Q8.B
  N21: R2.Pin_0, Q4.B
  N22: Q4.E, LED_PWM.pin4
  N23: Q4.C, LED_PWM.pin3
  N24: Q5.E, LED_PWM.pin6
  N25: Q5.B, R5.Pin_0
  N26: Q5.C, LED_PWM.pin5
  N27: Q6.E, LED_PWM.pin2
  N28: Q6.B, R4.Pin_0
  N29: Q6.C, LED_PWM.pin1
  N30: 24v.pin1, Case_Fan.pin2, LED_Fan.pin2
  N31: DMX.pin1, U1.B
  N32: DMX.pin2, U1.A
  N33: Case_Fan.pin1, Q7.C
  N34: Q7.B, R10.Pin_0
  N35: LED_Fan.pin5, Q8.C

notes:
  5V CMD SD3 SD2 G13 GND G12 G14 G27 G26 G25 G33 G32 G35 G34  SN  SP  EN  3v3
  CLK SD0 SD1 G15 G2  G0  G4  G16 G17 G5 G18 G19 GND G21 RXD TXD G22 G23 GND
